# Fritzing sketch LightningDetector1 (saved by Fritzing 0.8.5b)
circuit board: 8cm x 5cm
breadboards: 1

parts:
  D2 = Schottky Diode [part_number=1N5817 package="300 mil [THT]"]
  D1 = Zener Diode [part_number=NZX6V8D breakdown_voltage=6.8V package="300 mil [THT]"]
  U1 = atmega328 [package=dip]
  IC1 = Voltage Regulator [package=to-92]
  C1 = Ceramic Capacitor [capacitance=1µF package="100 mil [THT, multilayer]"]
  C2 = Ceramic Capacitor [capacitance=2.2µF package="100 mil [THT, multilayer]"]
  R1 = Resistor [tolerance=±5% resistance=22k package=THT]
  Y1_16MHz = CRYSTAL [package=hc49us]
  C4 = Ceramic Capacitor [package="200 mil [THT, multilayer]"]
  C5 = Ceramic Capacitor [package="200 mil [THT, multilayer]"]
  C3 = Ceramic Capacitor [package="200 mil [THT, multilayer]"]
  Thunder_click_pins_9-16 = male pin header, 8 pins [form="♂ (male)"]
  GPS = male pin header, 4 pins [form="♂ (male)"]
  Thunder_click_pins_1-8 = male pin header, 8 pins [form="♂ (male)"]
  J2 = Screw terminal - 2 pins [package=THT]
  J6 = Screw terminal - 2 pins [package=THT]
  SDI12 = male pin header, 3 pins [form="♂ (male)"]

nets (from the schematic view):
  N1: D2.cathode, IC1.IN, C1.1, J2.pin1
  N2: D2.anode, D1.cathode, J6.pin1
  GND: D1.anode, U1.GND#21, IC1.GND, C1.0, C4.0, C5.0, C3.0, Thunder_click_pins_9-16.pin1, GPS.pin2, Thunder_click_pins_1-8.pin8, J2.pin2, J6.pin2, SDI12.pin3
  N3: U1.RESET, R1.Pin_1
  N4: U1.D1_(TX), SDI12.pin2
  N5: U1.VCC, U1.AVCC, IC1.OUT, C2.1, R1.Pin_0, C3.1, GPS.pin1, Thunder_click_pins_1-8.pin2, SDI12.pin1
  N6: U1.GND#7, C2.0
  N7: U1.XLAT1, Y1_16MHz.2, C4.1
  N8: U1.XLAT2, Y1_16MHz.1, C5.1
  N9: U1.D7, GPS.pin3
  N10: U1.D8, GPS.pin4
  N11: U1.D9_(PWM), Thunder_click_pins_9-16.pin7
  N12: U1.D10_(PWM), Thunder_click_pins_1-8.pin6
  N13: U1.D11_(PWM), Thunder_click_pins_1-8.pin3
  N14: U1.D12, Thunder_click_pins_1-8.pin4
  N15: U1.D13, Thunder_click_pins_1-8.pin5

notes:
  solar
  battery
  GPS
  +
  -
  rx
  tx
  ATMega328
  1
  14
  15
  28
  Thunder
  click
  TAHMO
  Lightning
  Detector
  Hackaday
  v0.1 29JUL15
  Team TAHMO Hackaday, Lightning Detector w/ ATMega328, solar power, 0.2

custom parts:
  Voltage Regulator: Voltage Regulator LP2950 TI
  Ceramic Capacitor: 100 nF multilayer Ceramic Capacitor
